# Fritzing sketch laoyout (saved by Fritzing 0.9.3b)
breadboards: 1

parts:
  Raspberry_Pi1 = Raspberry Pi B rev2
  S1 = Pushbutton [package="[SMD]"]
  LED1 = LED - 5mm [color="Blue (470nm)" package="5 mm [THT]"]
  R1 = Resistor [tolerance=±5% resistance=220 package=THT]
  S2 = Pushbutton [package="[SMD]"]
  LED2 = LED - 5mm [color="Blue (470nm)" package="5 mm [THT]"]
  S3 = Pushbutton [package="[SMD]"]
  LED3 = LED - 5mm [color="Blue (470nm)" package="5 mm [THT]"]
  S4 = Pushbutton [package="[SMD]"]
  LED4 = LED - 5mm [color="Blue (470nm)" package="5 mm [THT]"]
  R2 = Resistor [tolerance=±5% resistance=220 package=THT]
  R3 = Resistor [tolerance=±5% resistance=220 package=THT]
  R4 = Resistor [tolerance=±5% resistance=220 package=THT]

nets:
  N1: Raspberry_Pi1.GPIO_3, S2.Pin_3, S2.Pin_4
  N2: Raspberry_Pi1.GND, S1.Pin_1, S1.Pin_2, R1.Pin_1, S2.Pin_1, S2.Pin_2, S3.Pin_1, S3.Pin_2, S4.Pin_1, S4.Pin_2, R2.Pin_1, R3.Pin_1, R4.Pin_1
  N3: Raspberry_Pi1.GPIO_23, S4.Pin_3, S4.Pin_4
  N4: Raspberry_Pi1.GPIO_14, LED1.anode
  N5: Raspberry_Pi1.GPIO_15, S1.Pin_3, S1.Pin_4
  N6: Raspberry_Pi1.GPIO_17, S3.Pin_3, S3.Pin_4
  N7: Raspberry_Pi1.GPIO_18, LED4.anode
  N8: Raspberry_Pi1.GPIO_4, LED3.anode
  N9: LED1.cathode, R1.Pin_0
  N10: LED2.cathode, R2.Pin_0
  N11: LED3.cathode, R3.Pin_0
  N12: LED4.cathode, R4.Pin_0
